# Fritzing sketch HistoRdualESP32 (saved by Fritzing 0.9.3b)
circuit board: 15.96cm x 9.95785cm
breadboards: 1

parts:
  U1 = LuaNode32 / ESP32 [part_number=ESP32S-PIN30]
  U2 = LuaNode32 / ESP32 [part_number=ESP32S-PIN30]
  microSD1 = MicroSD Card Module  # not connected
  PCM5102A_I2S_Stereo_DAC1 = PCM5102A I2S Stereo DAC  # not connected
  FMradio = Digital FM Radio Receiver  # not connected
  FMtransmitter = Si4713 Stereo FM Transmitter  # not connected
  Součástka1 = MCU5102 I2S Stereo DAC  # not connected
  MCU5102_I2S_Stereo_DAC1_1 = MCU5102 I2S Stereo DAC  # not connected
  MCU5102_I2S_Stereo_DAC1_2 = MCU5102 I2S Stereo DAC  # not connected
  MCU5102_I2S_Stereo_DAC1_3 = MCU5102 I2S Stereo DAC  # not connected
  MCU5102_I2S_Stereo_DAC1_4 = MCU5102 I2S Stereo DAC  # not connected
  MCU5102_I2S_Stereo_DAC2 = MCU5102 I2S Stereo DAC
  MCU5102_I2S_Stereo_DAC1 = MCU5102 I2S Stereo DAC

nets:
  GND: U1.GND, U2.GND
  N1: MCU5102_I2S_Stereo_DAC2.connector0, MCU5102_I2S_Stereo_DAC1.connector0

custom parts:
  LuaNode32 / ESP32: New Image for LuaNode32 DOIT ESP32 DEVKIT V1. Base parts from LuaNode32 / ESP32 ESP32 based LuaNode32 by G.Noorlander DOIT Esp32 DevKit v1 (30 pins long, 11 pins width) by Werner Rothschopf (modified by vanepp Dec 2018)
  Si4713 Stereo FM Transmitter: Yaaar! Become your very own pirate radio station with this FM radio transmitter. This breakout board, based on the best-of-class Si4713, is an all-in-one stereo audio FM transmitter that can also transmit RDS/RBDS data!
